// Logisim project projeto-ula.circ as structural Verilog: 3 circuits, main circuit main
module main (
  input  in_1,
  input  [7:0] in_2,
  input  in_3,
  input  [7:0] in_4,
  input  [3:0] in_5,
  output [2:0] out_6,
  output [7:0] out_7
);

  wire [7:0] aula_20_04_1_p3, divisor_1_out_3, divisor_1_out_4, result, somador_1_out_4, somador_2_out_4;

  // cont7 cont7_1: pin names not known
  // ula_main main_1: pin names not known; wires that end beside it: in_3, out_6, in_1, out_6, result, out_7
  somador somador_1 (.in_1(in_2), .in_2(in_4), .in_3(1'b0), .out_4(somador_1_out_4));  // open: out_5
  somador somador_2 (.in_1(in_2), .in_2(in_4), .in_3(1'b1), .out_4(somador_2_out_4));  // open: out_5
  divisor divisor_1 (.out_3(divisor_1_out_3), .out_4(divisor_1_out_4), .in_1(in_2), .in_2(in_4));
  // aula_20_04 aula_20_04_1: pin names not known; wires that end beside it: in_2, in_4, aula_20_04_1_p3
  Multiplexer #(.select(4), .width(8), .enable("false")) multiplexer_1 (
    .in0(somador_1_out_4), .in1(somador_2_out_4), .in2(divisor_1_out_4), .in3(aula_20_04_1_p3),
    .in4(divisor_1_out_3), .out(result), .sel(in_5));  // open: in5, in6, in7, in8, in9, in10, in11, in12, in13, in14, in15

  // Other names for the same wires on the sheet: n1[7:0] = in_2; n2[7:0] = in_4

  // Notes on the sheet:
  //   adição
  //   subtração
  //   divisão
  //   multiplicação
endmodule

module novo (
  input  [7:0] in_1,
  input  [7:0] in_2,
  input  \mudar_posiçao ,
  input  [3:0] \Operação ,
  input  Gravar,
  input  [7:0] in_6,
  output [2:0] \Posição ,
  output [7:0] out_8
);

  wire [3:0] display_1_out_3, display_1_out_4;

  display display_1 (.in_1(out_8), .in_2(in_6), .out_3(display_1_out_3), .out_4(display_1_out_4));
  Hex_Digit_Display hex_digit_display_1 (.value(display_1_out_4));  // open: dp
  Hex_Digit_Display hex_digit_display_2 (.value(display_1_out_3));  // open: dp
  main main_1 (
    .in_1(Gravar), .in_2(in_1), .in_3(\mudar_posiçao ), .in_4(in_2), .out_6(\Posição ), .out_7(out_8),
    .in_5(\Operação ));

  // Other names for the same wires on the sheet: Memória[7:0] = out_8

  // Notes on the sheet:
  //   OPERAÇÕES
  //   0000 -  Adição
  //   0001 -  Subtração
  //   0010 - Divisão
  //   0011 - Multiplicação
  //   0100 - Resto da Divisão
  //   Numero 1
  //   Numero 2
  //   Memória
endmodule

module display (
  input  [7:0] in_1,
  input  [7:0] in_2,
  output [3:0] out_3,
  output [3:0] out_4
);

  wire [7:4] divider_1_out, divider_1_rem;

  Divider divider_1 (.a(in_1), .b(in_2), .out({divider_1_out, out_3}), .rem({divider_1_rem, out_4}));  // open: upper
endmodule
